// Logisim project Trabalho-mata-38.circ as structural Verilog: 4 circuits, main circuit ULA
module main (
  input  [3:0] Rd,
  input  [3:0] Rin,
  input  [3:0] Rs1,
  input  [3:0] Rs2,
  input  [3:0] OP,
  input  rw_ctl,
  input  [7:0] in_7,
  input  [7:0] in_8,
  input  in_9,
  input  in_10,
  input  in_11,
  output [11:0] out_12,
  output [7:0] OUT,
  output R0
);

  wire clock_1_out, reset;
  wire [7:0] counter_1_q, Rx, Ry;

  Button button_1 (.out(reset));
  CTLU ctlu_1 ();  // open: R0, Op, rw_ctl
  Clock clock_1 (.out(clock_1_out));
  Counter #(.max('hf)) counter_1 (.Q(counter_1_q), .clk(clock_1_out), .clr(reset));  // open: load, D, count, carry
  ULA ula_1 (.Ix(Rx), .Iy(Ry), .OUT(OUT), .OP(OP));
  ROM #(.dataWidth(12)) rom_1 (.addr(counter_1_q), .data(out_12));  // open: sel
  RAM ram_1 (.addr(in_7), .data(in_8), .clk(in_10), .ld(in_11));  // open: sel, clr
  REGs regs_1 (.Rx(Rx), .Ry(Ry), .Rd(Rd), .rw_clt(rw_ctl), .Rs2(Rs2), .Rs1(Rs1), .R0(R0), .Rin(Rin), .reset(reset));

  // Notes on the sheet:
  //   IM
  //   contents of rom_1 (hex, n*v repeats v):
  //   b00 d10 b0a d20 b01 d30 812 200 e0d 331 d10 b01 e06 d01 c00 f00
  //   DM
  //   0000 AND (BIT A BIT)
  //   0001 OR (BIT A BIT)
  //   0010 NÃO LÓGICO
  //   0011 ADIÇÃO
  //   0100 SUBTRAÇÃO
  //   0101 MULTIPLICAÇÃO
  //   0110 DIVISÃO
  //   0111 IGUAL 
  //   1000 MENOR
  //   1111 PARAR
  //   1001MENOR OU IGUAL
  //   1010 LER DA MEMORIA
  //   1011 LER DA IMEDIATO
  //   1100 ARMAZENAR NA MEMÓRIA
  //   1101 COPIAR REGISTRADOR
  //   1110 DESVIO DE FLUXO
endmodule

module ULA (
  input  [7:0] Ix,
  input  [7:0] Iy,
  input  [3:0] OP,
  output [7:0] OUT
);

  wire comparator_1_eq, comparator_1_lt, not_1_out, or_2_out, or_3_out;
  wire [7:0] adder_1_out, and_1_out, bit_extender_1_out, bit_extender_2_out, bit_extender_3_out,
       bit_extender_4_out, divider_1_out, multiplier_1_out, or_1_out, subtractor_1_out;

  assign and_1_out = Ix & Iy;  // AND_Gate and_1, 8 bits wide
  assign or_1_out = Ix | Iy;  // OR_Gate or_1, 8 bits wide
  or or_2 (or_2_out, Ix[0], Ix[1], Ix[2], Ix[3], Ix[4], Ix[5], Ix[6], Ix[7]);
  Adder adder_1 (.a(Ix), .b(Iy), .out(adder_1_out));  // open: cin, cout
  Subtractor subtractor_1 (.a(Ix), .b(Iy), .out(subtractor_1_out));  // open: bin, bout
  Multiplier multiplier_1 (.a(Ix), .b(Iy), .out(multiplier_1_out));  // open: cin, cout
  Divider divider_1 (.a(Ix), .b(Iy), .out(divider_1_out));  // open: upper, rem
  Comparator comparator_1 (.a(Ix), .b(Iy), .eq(comparator_1_eq), .lt(comparator_1_lt));  // open: gt
  assign bit_extender_1_out = {{7{1'b0}}, not_1_out};  // Bit_Extender bit_extender_1
  not not_1 (not_1_out, or_2_out);
  assign bit_extender_2_out = {{7{1'b0}}, comparator_1_eq};  // Bit_Extender bit_extender_2
  assign bit_extender_3_out = {{7{1'b0}}, comparator_1_lt};  // Bit_Extender bit_extender_3
  or or_3 (or_3_out, comparator_1_lt, comparator_1_eq);
  Multiplexer #(.select(4), .width(8)) multiplexer_1 (
    .in0(and_1_out), .in1(or_1_out), .in2(bit_extender_1_out), .in3(adder_1_out), .in4(subtractor_1_out),
    .in5(multiplier_1_out), .in6(divider_1_out), .in7(bit_extender_2_out), .in8(bit_extender_3_out),
    .in9(bit_extender_4_out), .out(OUT), .sel(OP));  // open: in10, in11, in12, in13, in14, in15, en
  assign bit_extender_4_out = {{7{1'b0}}, or_3_out};  // Bit_Extender bit_extender_4
endmodule

module REGs (
  input  [3:0] Rs2,
  input  [3:0] Rs1,
  input  [3:0] Rd,
  input  [3:0] Rin,
  input  reset,
  input  rw_clt,
  output [7:0] Rx,
  output [7:0] Ry,
  output R0
);

  wire clock_1_out, demultiplexer_1_out0, demultiplexer_1_out1, demultiplexer_2_out0, demultiplexer_2_out1,
       demultiplexer_2_out2, demultiplexer_2_out3, demultiplexer_2_out4, demultiplexer_2_out5,
       demultiplexer_2_out6, demultiplexer_2_out7, demultiplexer_2_out8, demultiplexer_2_out9,
       demultiplexer_2_out10, demultiplexer_2_out11, demultiplexer_2_out12, demultiplexer_2_out13,
       demultiplexer_2_out14, demultiplexer_2_out15;
  wire [7:0] bit_extender_1_out, multiplexer_1_out, multiplexer_2_out, R0_q, R1_q, R2_q, R3_q, R4_q, R5_q,
       R6_q, R7_q, R8_q, R9_q, R10_q, R11_q, R12_q, R13_q, R14_q, R15_q;

  Demultiplexer demultiplexer_1 (
    .out0(demultiplexer_1_out0), .out1(demultiplexer_1_out1), .in(1'b1), .sel(rw_clt));  // open: en
  Multiplexer #(.width(8), .enable("false")) multiplexer_1 (
    .in0({Rd, Rin}), .out(multiplexer_1_out), .sel(demultiplexer_1_out0));  // open: in1
  Multiplexer #(.width(8), .enable("false")) multiplexer_2 (
    .in0({Rs2, Rs1}), .out(multiplexer_2_out), .sel(demultiplexer_1_out1));  // open: in1
  Clock clock_1 (.out(clock_1_out));
  Demultiplexer #(.select(4)) demultiplexer_2 (
    .out0(demultiplexer_2_out0), .out1(demultiplexer_2_out1), .out2(demultiplexer_2_out2),
    .out3(demultiplexer_2_out3), .out4(demultiplexer_2_out4), .out5(demultiplexer_2_out5),
    .out6(demultiplexer_2_out6), .out7(demultiplexer_2_out7), .out8(demultiplexer_2_out8),
    .out9(demultiplexer_2_out9), .out10(demultiplexer_2_out10), .out11(demultiplexer_2_out11),
    .out12(demultiplexer_2_out12), .out13(demultiplexer_2_out13), .out14(demultiplexer_2_out14),
    .out15(demultiplexer_2_out15), .in(clock_1_out), .sel(multiplexer_1_out[7:4]));  // open: en
  Multiplexer #(.select(4), .width(8)) multiplexer_3 (
    .in0(R0_q), .in1(R1_q), .in2(R2_q), .in3(R3_q), .in4(R4_q), .in5(R5_q), .in6(R6_q), .in7(R7_q),
    .in8(R8_q), .in9(R9_q), .in10(R10_q), .in11(R11_q), .in12(R12_q), .in13(R13_q), .in14(R14_q),
    .in15(R15_q), .out(Rx), .sel(multiplexer_2_out[3:0]));  // open: en
  Multiplexer #(.select(4), .width(8)) multiplexer_4 (
    .in0(R0_q), .in1(R1_q), .in2(R2_q), .in3(R3_q), .in4(R4_q), .in5(R5_q), .in6(R6_q), .in7(R7_q),
    .in8(R8_q), .in9(R9_q), .in10(R10_q), .in11(R11_q), .in12(R12_q), .in13(R13_q), .in14(R14_q),
    .in15(R15_q), .out(Ry), .sel(multiplexer_2_out[7:4]));  // open: en
  assign bit_extender_1_out = {{4{1'b0}}, multiplexer_1_out[3:0]};  // Bit_Extender bit_extender_1
  Register u_R0 (.D(bit_extender_1_out), .Q(R0_q), .clk(demultiplexer_2_out0), .clr(reset));  // open: en
  Register R8 (.D(bit_extender_1_out), .Q(R8_q), .clk(demultiplexer_2_out8), .clr(reset));  // open: en
  Register R1 (.D(bit_extender_1_out), .Q(R1_q), .clk(demultiplexer_2_out1), .clr(reset));  // open: en
  Register R9 (.D(bit_extender_1_out), .Q(R9_q), .clk(demultiplexer_2_out9), .clr(reset));  // open: en
  Register R2 (.D(bit_extender_1_out), .Q(R2_q), .clk(demultiplexer_2_out2), .clr(reset));  // open: en
  Register R10 (.D(bit_extender_1_out), .Q(R10_q), .clk(demultiplexer_2_out10), .clr(reset));  // open: en
  Register R3 (.D(bit_extender_1_out), .Q(R3_q), .clk(demultiplexer_2_out3), .clr(reset));  // open: en
  Register R11 (.D(bit_extender_1_out), .Q(R11_q), .clk(demultiplexer_2_out11), .clr(reset));  // open: en
  Register R4 (.D(bit_extender_1_out), .Q(R4_q), .clk(demultiplexer_2_out4), .clr(reset));  // open: en
  Register R12 (.D(bit_extender_1_out), .Q(R12_q), .clk(demultiplexer_2_out12), .clr(reset));  // open: en
  Register R5 (.D(bit_extender_1_out), .Q(R5_q), .clk(demultiplexer_2_out5), .clr(reset));  // open: en
  Register R13 (.D(bit_extender_1_out), .Q(R13_q), .clk(demultiplexer_2_out13), .clr(reset));  // open: en
  Register R6 (.D(bit_extender_1_out), .Q(R6_q), .clk(demultiplexer_2_out6), .clr(reset));  // open: en
  Register R14 (.D(bit_extender_1_out), .Q(R14_q), .clk(demultiplexer_2_out14), .clr(reset));  // open: en
  Register R7 (.D(bit_extender_1_out), .Q(R7_q), .clk(demultiplexer_2_out7), .clr(reset));  // open: en
  Register R15 (.D(bit_extender_1_out), .Q(R15_q), .clk(demultiplexer_2_out15), .clr(reset));  // open: en
  or or_1 (R0, R0_q[0], R0_q[1], R0_q[2], R0_q[3], R0_q[4], R0_q[5], R0_q[6], R0_q[7]);
endmodule

module CTLU (
  input  [3:0] Op,
  input  R0,
  output rw_ctl
);

  wire [7:0] multiplexer_1_out, undriven, undriven_2, undriven_3, undriven_4, undriven_5, undriven_6;

  Demultiplexer #(.enable("false")) demultiplexer_1 (.sel(R0));  // open: out0, out1, in
  Multiplexer #(.select(4), .width(8), .enable("false")) multiplexer_1 (
    .in10(undriven_6), .in11(undriven_4), .in12(undriven_2), .in13(undriven_3), .in14(undriven),
    .in15(undriven_5), .out(multiplexer_1_out), .sel(Op));  // open: in0, in1, in2, in3, in4, in5, in6, in7, in8, in9
  or or_1 (rw_ctl, undriven[0], undriven[1], undriven[2], undriven[3], undriven[4], undriven[5], undriven[6], undriven[7]);
endmodule
